// Logisim project cpu.circ as structural Verilog: 1 circuit, main circuit cpu
module cpu (
  input  clk,
  input  [31:0] Instruction,
  input  [31:0] MemReadData,
  output [31:0] MemAddress,
  output [31:0] ProgramCounter,
  output [31:0] ra,
  output [31:0] sp,
  output [31:0] t0,
  output [31:0] t1,
  output [31:0] t2,
  output [31:0] s0,
  output [31:0] s1,
  output [31:0] a0,
  output [3:0] MemWriteMask,
  output [31:0] MemWriteData
);

  wire BSEL, REGWEN;
  wire [2:0] IMMSEL;
  wire [3:0] ALUSEL;
  wire [31:0] adder_1_out, ALUout, IMM, multiplexer_1_out, READ1, READ2;

  Register #(.width(32)) PC (.D(adder_1_out), .clk(clk), .Q(ProgramCounter));  // open: en, clr
  Adder #(.width(32)) adder_1 (.a(ProgramCounter), .b(32'h4), .out(adder_1_out));  // open: cin, cout
  control_logic control_logic_1 (
    .RegWEn(REGWEN), .ImmSel(IMMSEL), .BSel(BSEL), .ALUSel(ALUSEL), .Instruction(Instruction));  // open: PCSel, BrUn, ASel, MemWEn, WBSel, BrEq, BrLt
  regfile regfile_1 (
    .ReadIndex1(Instruction[19:15]), .ReadIndex2(Instruction[24:20]), .WriteIndex(Instruction[11:7]),
    .WriteData(ALUout), .RegWEn(REGWEN), .clk(clk), .ra(ra), .sp(sp), .t0(t0), .t1(t1), .t2(t2), .s0(s0),
    .s1(s1), .a0(a0), .ReadData1(READ1), .ReadData2(READ2));
  imm_gen imm_gen_1 (.Instruction(Instruction), .ImmSel(IMMSEL), .Immediate(IMM));
  Multiplexer #(.width(32)) multiplexer_1 (.in0(READ2), .in1(IMM), .out(multiplexer_1_out), .sel(BSEL));
  alu alu_1 (.ALUResult(ALUout), .A(READ1), .B(multiplexer_1_out), .ALUSel(ALUSEL));
  // branch_comp branch_comp_1: pin names not known
  // partial_store partial_store_1: pin names not known
  // partial_load partial_load_1: pin names not known

  // Other names for the same wires on the sheet: RD[4:0] = Instruction[11:7]; RS1[4:0] = Instruction[19:15];
  //   RS2[4:0] = Instruction[24:20]

  // Notes on the sheet:
  //   To IMEM
  //   IMEM (do **NOT** move this)
  //   From IMEM
  //   Inputs/Outputs for testing. Do **NOT** move these.
  //   It is OK to move the PC, RegFile, ALU, MEM, Branch Comp, Imm Gen, Partial Load, Partial Store and Control Logic to wherever is most convenient for you when constructing your CPU, and to delete this text
  //   To DMEM
  //   DMEM (do **NOT** move this)
  //   From DMEM
endmodule
